# Fritzing sketch See n Say-circuit (saved by Fritzing 0.9.3b)

parts:
  Part1 = Adafruit Metro Mini [part_number="Adafruit #2590"]
  S1 = Taiway 100-SP-X-T1 SPDT Miniature Toggle Switch [part_number=100-SP-X-T1-0-0-B1-M1 package=THT]
  BAT1 = Battery Holders [package=battery-aa]
  BAT2 = Battery Holders [package=battery-aa]
  BAT3 = Battery Holders [package=battery-aa]
  BAT4 = Battery Holders [package=battery-aa]
  BAT5 = Battery Holders [package=battery-aa]
  J1 = Basic Servo
  Part2 = NRF24L01+ Breakout Board
  D2F2 = D2F-FL Omron Snap Action Limit Switch with Level

nets:
  N1: Part1.IO13, Part2.SCK
  N2: Part1.IO12, Part2.MISO
  N3: Part1.IO11, Part2.MOSI
  N4: Part1.IO10, D2F2.NO
  N5: Part1.IO9, J1.pulse
  N6: Part1.IO8, Part2.CS
  N7: Part1.IO7, Part2.CE
  3.3V: Part1.3.3V, Part2.VCC
  +5V: Part1.+5V, J1.vcc
  GND: Part1.GND, BAT5.+, J1.gnd, Part2.GND, D2F2.COM
  N8: Part1.VIN, S1.L2
  N9: S1.COM, BAT1.-
  N10: BAT1.+, BAT2.-
  N11: BAT2.+, BAT3.-
  N12: BAT3.+, BAT4.-
  N13: BAT4.+, BAT5.-

custom parts:
  Adafruit Metro Mini: We sure love the ATmega328 here at Adafruit, and we use them a lot for our own projects. The processor has plenty of GPIO, Analog inputs, hardware UART SPI and I2C, timers and PWM galore - just enough for most simple projects. When we need to go small, we use a Pro Trinket 3V or 5V, but if you want to have USB-to-Serial built in, we reach for an Adafruit METRO Mini. METRO Mini is the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
  D2F-FL Omron Snap Action Limit Switch with Level: Snap action switch with stainless steel lever.
