# Fritzing sketch Speak and Spell (saved by Fritzing 0.9.3b)

parts:
  Part2 = Arduino Mega Proto Shield (v6)
  Part3 = NRF24L01+ Breakout Board
  S1 = Taiway 100-SP-X-T1 SPDT Miniature Toggle Switch [part_number=100-SP-X-T1-0-0-B1-M1 package=THT]
  U1 = LCD-16X2 [package=lcd-16x2_nosilk]
  R1 = Resistor [tolerance=±5% resistance=10k package="2512 [SMD]"]
  BAT1 = BC9VPC [package=bc9vpc]
  BAT2 = BC9VPC [package=bc9vpc]
  SP1 = SPEAKER [package=pcb_mount_speaker]
  KEYBOARD_MATRIX = M16 [package=1x16_machine-pin-header_lock.004]

nets:
  +5V: Part2.+5V, U1.VDD, U1.K
  N1: Part2.GND, U1.A
  N2: Part2.D2, U1.DB7
  N3: Part2.D3, U1.DB6
  N4: Part2.D4, U1.DB5
  N5: Part2.D5, U1.DB4
  N6: Part2.D6, U1.E
  N7: Part2.D7, U1.RS
  N8: Part2.D12, SP1.+
  N9: Part2.D9, Part3.CE
  +3V3: Part2.+3V3, Part3.VCC
  N10: Part2.D25, KEYBOARD_MATRIX.12
  N11: Part2.D27, KEYBOARD_MATRIX.3
  N12: Part2.D34, KEYBOARD_MATRIX.10
  N13: Part2.D50, Part3.MISO
  N14: Part2.D51, Part3.MOSI
  N15: Part2.D52, Part3.SCK
  N16: Part2.D53, Part3.CS
  N17: Part2.D22, KEYBOARD_MATRIX.1
  N18: Part2.D23, KEYBOARD_MATRIX.2
  N19: Part2.D24, KEYBOARD_MATRIX.11
  N20: Part2.D26, KEYBOARD_MATRIX.13
  N21: Part2.D28, KEYBOARD_MATRIX.4
  N22: Part2.D29, KEYBOARD_MATRIX.5
  N23: Part2.D30, KEYBOARD_MATRIX.6
  N24: Part2.D31, KEYBOARD_MATRIX.7
  N25: Part2.D32, KEYBOARD_MATRIX.8
  N26: Part2.D33, KEYBOARD_MATRIX.9
  N27: Part2.+9V, S1.COM
  N28: Part2.N$70, Part3.GND
  N29: Part2.N$118, U1.R_W, R1.Pin_0, BAT1.V-, BAT2.V-, SP1.-
  N30: Part2.N$470, U1.VSS
  N31: S1.L2, BAT1.V+, BAT2.V+
  N32: U1.VO, R1.Pin_1

notes:
  10k Resistor either to GND or +5V
